# Fritzing sketch victoria (saved by Fritzing 0.9.2b)
circuit board: 8.46667cm x 5.64444cm
breadboards: 2

parts:
  Arduino = Arduino Mega 2560 (Rev3)
  Q1 = Basic FET N-Channel [package="TO220 [THT]"]
  R1 = Resistor [tolerance=±5% resistance=100 package=THT]
  R2 = Resistor [tolerance=±5% resistance=10k package=THT]
  GPS = double row male pin header, 6 pins [form="♂ (male)"]
  Power = Header 2 [package=screwterminal-3.5mm-2_lock]
  Q2 = Basic FET N-Channel [package="TO220 [THT]"]
  R3 = Resistor [tolerance=±5% resistance=100 package=THT]
  R4 = Resistor [tolerance=±5% resistance=10k package=THT]
  RF = double row male pin header, 8 pins [form="♂ (male)"]
  RTC = male pin header, 4 pins [form="♂ (male)"]
  Q3 = Basic FET N-Channel [package="TO220 [THT]"]
  R5 = Resistor [tolerance=±5% resistance=100 package=THT]
  R6 = Resistor [tolerance=±5% resistance=10k package=THT]
  Q4 = Basic FET N-Channel [package="TO220 [THT]"]
  R7 = Resistor [tolerance=±5% resistance=100 package=THT]
  R8 = Resistor [tolerance=±5% resistance=10k package=THT]
  R9 = Resistor [tolerance=±5% resistance=4.7k package=THT]
  Temp = male pin header, 3 pins [form="♂ (male)"]
  Motor_Draw = male pin header, 3 pins [form="♂ (male)"]
  Q5 = Basic FET N-Channel [package="TO220 [THT]"]
  R10 = Resistor [tolerance=±5% resistance=100 package=THT]
  R11 = Resistor [tolerance=±5% resistance=10k package=THT]
  Q6 = Basic FET N-Channel [package="TO220 [THT]"]
  R12 = Resistor [tolerance=±5% resistance=100 package=THT]
  R13 = Resistor [tolerance=±5% resistance=10k package=THT]
  PHOTO = male pin header, 3 pins [form="♂ (male)"]
  R14 = Resistor [tolerance=±5% resistance=10k package=THT]
  Q7 = Basic FET N-Channel [package="TO220 [THT]"]
  R15 = Resistor [tolerance=±5% resistance=100 package=THT]
  R16 = Resistor [tolerance=±5% resistance=10k package=THT]
  Lightening = male pin header, 7 pins [form="♂ (male)"]
  RockBlock = male pin header, 5 pins [form="♂ (male)"]
  Q8 = Basic FET N-Channel [package="TO220 [THT]"]
  R17 = Resistor [tolerance=±5% resistance=100 package=THT]
  R18 = Resistor [tolerance=±5% resistance=10k package=THT]
  accel = male pin header, 6 pins [form="♂ (male)"]
  Motor = Screw terminal - 2 pins [package=THT]
  R19 = Resistor [tolerance=±5% resistance=100 package=THT]
  R20 = Resistor [tolerance=±5% resistance=100 package=THT]
  ESC = screw terminal, 3 pins

nets:
  N1: Arduino.A8, Motor_Draw.pin2
  N2: Arduino.A2, accel.pin4
  N3: Arduino.A3, accel.pin5
  N4: Arduino.A4, accel.pin6
  N5: Arduino.A5, PHOTO.pin2, R14.Pin_0
  N6: Arduino.D21/SCL, GPS.pin6, RTC.pin4, Lightening.pin4
  N7: Arduino.D20/SDA, GPS.pin5, RTC.pin3, Lightening.pin6
  N8: Arduino.D17_PWM/RX2, RockBlock.pin4
  N9: Arduino.D16_PWM/TX2, RockBlock.pin3
  N10: Arduino.D15/RX3, GPS.pin2
  N11: Arduino.D14/TX3, GPS.pin3
  N12: Arduino.D11_PWM, ESC.pin1
  N13: Arduino.D10_PWM, ESC.pin2
  N14: Arduino.D9_PWM, ESC.pin3
  N15: Arduino.5V, PHOTO.pin1, Lightening.pin1, RockBlock.pin1, accel.pin1
  N16: Arduino.GND, Q1.source, R2.Pin_1, Power.2, Q2.source, R4.Pin_1, Q3.source, R6.Pin_1, Q4.source, R8.Pin_1, Q5.source, R11.Pin_1, Q6.source, R13.Pin_1, Q7.source, R16.Pin_1, RockBlock.pin2, Q8.source, R18.Pin_1
  N17: Arduino.VIN, GPS.pin1, Power.1, RF.pin1, RTC.pin2, R9.Pin_0, Temp.pin1, Motor_Draw.pin1
  N18: Arduino.D2_PWM, R9.Pin_1, Temp.pin2
  N19: Arduino.D23, R5.Pin_0
  N20: Arduino.D24, R1.Pin_0
  N21: Arduino.D26, RockBlock.pin5
  N22: Arduino.D31, R19.Pin_0
  N23: Arduino.D32, R17.Pin_0
  N24: Arduino.D33, R20.Pin_0
  N25: Arduino.D36, R7.Pin_0
  N26: Arduino.D40, R12.Pin_0
  N27: Arduino.D41, R3.Pin_0
  N28: Arduino.D44, R10.Pin_0
  N29: Arduino.D46, R15.Pin_0
  N30: Arduino.D48, RF.pin7
  N31: Arduino.D49, RF.pin2
  N32: Arduino.D50, RF.pin5
  N33: Arduino.D51, RF.pin3
  N34: Arduino.D52, RF.pin6
  N35: Q1.gate, R1.Pin_1, R2.Pin_0
  N36: Q1.drain, GPS.pin4
  N37: Q2.gate, R3.Pin_1
  N38: Q2.drain, R4.Pin_0, RF.pin8
  N39: RTC.pin1, Q3.drain, R6.Pin_0
  N40: Q3.gate, R5.Pin_1
  N41: Q4.gate, R7.Pin_1
  N42: Q4.drain, R8.Pin_0, Temp.pin3
  N43: Motor_Draw.pin3, Q5.drain, R11.Pin_0
  N44: Q5.gate, R10.Pin_1
  N45: Q6.gate, R12.Pin_1
  N46: Q6.drain, R13.Pin_0, PHOTO.pin3, R14.Pin_1
  N47: Q7.gate, R15.Pin_1
  N48: Q7.drain, R16.Pin_0, Lightening.pin7
  N49: Q8.gate, R17.Pin_1
  N50: Q8.drain, R18.Pin_0, accel.pin3
  N51: Motor.pin1, R19.Pin_1
  N52: Motor.pin2, R20.Pin_1
